// Logisim project ALU.circ as structural Verilog: 18 circuits, main circuit main
module main (
  input  [3:0] A,
  input  [3:0] OPERATION,
  input  [3:0] B,
  input  Zero_input,
  output [7:0] out_5,
  output zero_flag,
  output carry_borrow,
  output Overflow
);

  ALU alu_1 (
    .A(A), .B(B), .overflow(Zero_input), .in_1(OPERATION), .out_5(out_5), .out_6(zero_flag),
    .out_7(carry_borrow), .out_8(Overflow));

  // Notes on the sheet:
  //   Result
endmodule

// 2'sC
module _2_scomplement (
  input  D,
  input  C,
  input  B,
  input  A,
  output Z,
  output Y,
  output X,
  output W
);

  wire and_1_out, and_2_out, and_3_out, and_4_out, and_5_out, and_6_out, not_1_out, not_2_out, not_3_out,
       not_4_out, not_5_out, not_6_out, or_1_out, or_2_out;

  not not_1 (not_1_out, C);
  not not_2 (not_2_out, D);
  and and_1 (and_1_out, D, not_1_out);
  and and_2 (and_2_out, not_2_out, C);
  not not_3 (not_3_out, B);
  or or_1 (or_1_out, C, D);
  and and_3 (and_3_out, not_3_out, or_1_out);
  and and_4 (and_4_out, B, not_4_out);
  not not_4 (not_4_out, or_1_out);
  not not_5 (not_5_out, A);
  or or_2 (or_2_out, B, or_1_out);
  or or_3 (Y, and_1_out, and_2_out);
  not not_6 (not_6_out, or_2_out);
  or or_4 (X, and_3_out, and_4_out);
  and and_5 (and_5_out, not_5_out, or_2_out);
  and and_6 (and_6_out, A, not_6_out);
  or or_5 (W, and_5_out, and_6_out);

  assign Z = D;
endmodule

// And
module \and  (
  input  A0,
  input  A1,
  input  A2,
  input  A3,
  input  B0,
  input  B1,
  input  B2,
  input  B3,
  output W,
  output X,
  output Y,
  output Z
);

  and and_1 (W, A0, B0);
  and and_2 (X, A1, B1);
  and and_3 (Y, A2, B2);
  and and_4 (Z, A3, B3);
endmodule

// NAND
module \nand  (
  input  A0,
  input  A1,
  input  A2,
  input  A3,
  input  B0,
  input  B1,
  input  B2,
  input  B3,
  output W,
  output X,
  output Y,
  output Z
);

  wire and_1_out, and_2_out, and_3_out, and_4_out;

  and and_1 (and_1_out, A0, B0);
  not not_1 (W, and_1_out);
  not not_2 (X, and_2_out);
  and and_2 (and_2_out, A1, B1);
  and and_3 (and_3_out, A2, B2);
  not not_3 (Y, and_3_out);
  and and_4 (and_4_out, A3, B3);
  not not_4 (Z, and_4_out);
endmodule

// Or
module \or  (
  input  A0,
  input  A1,
  input  A2,
  input  A3,
  input  B0,
  input  B1,
  input  B2,
  input  B3,
  output W,
  output X,
  output Y,
  output Z
);

  or or_1 (W, A0, B0);
  or or_2 (X, A1, B1);
  or or_3 (Y, A2, B2);
  or or_4 (Z, A3, B3);
endmodule

// XOr
module \xor  (
  input  A0,
  input  A1,
  input  A2,
  input  A3,
  input  B0,
  input  B1,
  input  B2,
  input  B3,
  output W,
  output X,
  output Y,
  output Z
);

  wire and_1_out, and_2_out, and_3_out, and_4_out, and_5_out, and_6_out, and_7_out, and_8_out, not_1_out,
       not_2_out, not_3_out, not_4_out, not_5_out, not_6_out, not_7_out, not_8_out;

  not not_1 (not_1_out, B0);
  not not_2 (not_2_out, A0);
  not not_3 (not_3_out, B1);
  not not_4 (not_4_out, A1);
  not not_5 (not_5_out, B2);
  not not_6 (not_6_out, A2);
  not not_7 (not_7_out, B3);
  not not_8 (not_8_out, A3);
  and and_1 (and_1_out, not_1_out, A0);
  and and_2 (and_2_out, B0, not_2_out);
  and and_3 (and_3_out, not_3_out, A1);
  and and_4 (and_4_out, B1, not_4_out);
  and and_5 (and_5_out, not_5_out, A2);
  and and_6 (and_6_out, B2, not_6_out);
  and and_7 (and_7_out, not_7_out, A3);
  and and_8 (and_8_out, B3, not_8_out);
  or or_1 (W, and_1_out, and_2_out);
  or or_2 (X, and_3_out, and_4_out);
  or or_3 (Y, and_5_out, and_6_out);
  or or_4 (Z, and_7_out, and_8_out);
endmodule

// 1'sC
module _1_scomplement (
  input  A,
  input  B,
  input  C,
  input  D,
  output out_5,
  output out_6,
  output out_7,
  output out_8
);

  not not_1 (out_5, A);
  not not_2 (out_6, B);
  not not_3 (out_7, C);
  not not_4 (out_8, D);
endmodule

// ADD
module Add (
  input  carry,
  input  A0,
  input  A1,
  input  A2,
  input  A3,
  input  B0,
  input  B1,
  input  B2,
  input  B3,
  output out_10,
  output out_11,
  output out_12,
  output out_13,
  output Carry_2,
  output overflow
);

  wire and_1_out, and_2_out, and_3_out, and_4_out, and_5_out, and_6_out, and_7_out, and_8_out, and_9_out,
       and_10_out, and_11_out, and_12_out, and_13_out, and_14_out, and_15_out, and_16_out, and_17_out,
       and_18_out, and_19_out, and_20_out, and_21_out, and_22_out, and_23_out, and_24_out, and_25_out,
       and_26_out, not_1_out, not_2_out, not_3_out, not_4_out, not_5_out, not_6_out, not_7_out, not_8_out,
       not_9_out, not_10_out, not_11_out, not_12_out, not_13_out, not_14_out, not_15_out, not_16_out,
       not_17_out, not_18_out, or_1_out, or_2_out, or_3_out, or_4_out, or_5_out, or_6_out, or_7_out;

  not not_1 (not_1_out, B0);
  not not_2 (not_2_out, A0);
  not not_3 (not_3_out, B1);
  not not_4 (not_4_out, A1);
  not not_5 (not_5_out, B2);
  not not_6 (not_6_out, A2);
  not not_7 (not_7_out, B3);
  not not_8 (not_8_out, A3);
  and and_1 (and_1_out, A0, not_1_out);
  and and_2 (and_2_out, not_2_out, B0);
  and and_3 (and_3_out, A0, B0);
  and and_4 (and_4_out, A1, not_3_out);
  and and_5 (and_5_out, not_4_out, B1);
  and and_6 (and_6_out, A1, B1);
  and and_7 (and_7_out, A2, not_5_out);
  and and_8 (and_8_out, not_6_out, B2);
  and and_9 (and_9_out, A2, B2);
  and and_10 (and_10_out, A3, not_7_out);
  and and_11 (and_11_out, not_8_out, B3);
  and and_12 (and_12_out, A3, B3);
  or or_1 (or_1_out, and_1_out, and_2_out);
  or or_2 (or_2_out, and_4_out, and_5_out);
  or or_3 (or_3_out, and_7_out, and_8_out);
  or or_4 (or_4_out, and_10_out, and_11_out);
  and and_13 (and_13_out, carry, or_1_out);
  and and_14 (and_14_out, or_5_out, or_2_out);
  and and_15 (and_15_out, or_6_out, or_3_out);
  and and_16 (and_16_out, or_7_out, or_4_out);
  not not_9 (not_9_out, or_1_out);
  not not_10 (not_10_out, carry);
  or or_5 (or_5_out, and_13_out, and_3_out);
  not not_11 (not_11_out, or_2_out);
  not not_12 (not_12_out, or_5_out);
  or or_6 (or_6_out, and_14_out, and_6_out);
  not not_13 (not_13_out, or_3_out);
  not not_14 (not_14_out, or_6_out);
  or or_7 (or_7_out, and_15_out, and_9_out);
  not not_15 (not_15_out, or_4_out);
  not not_16 (not_16_out, or_7_out);
  or or_8 (Carry_2, and_16_out, and_12_out);
  and and_17 (and_17_out, carry, not_9_out);
  and and_18 (and_18_out, not_10_out, or_1_out);
  and and_19 (and_19_out, or_5_out, not_11_out);
  and and_20 (and_20_out, not_12_out, or_2_out);
  and and_21 (and_21_out, or_6_out, not_13_out);
  and and_22 (and_22_out, not_14_out, or_3_out);
  and and_23 (and_23_out, or_7_out, not_15_out);
  and and_24 (and_24_out, not_16_out, or_4_out);
  or or_9 (out_10, and_17_out, and_18_out);
  or or_10 (out_11, and_19_out, and_20_out);
  or or_11 (out_12, and_21_out, and_22_out);
  not not_17 (not_17_out, Carry_2);
  or or_12 (out_13, and_23_out, and_24_out);
  not not_18 (not_18_out, or_7_out);
  and and_25 (and_25_out, or_7_out, not_17_out);
  and and_26 (and_26_out, not_18_out, Carry_2);
  or or_13 (overflow, and_25_out, and_26_out);
endmodule

// SLL
module shift_left_logic (
  input  in_1,
  input  in_2,
  input  in_3,
  input  in_4,
  output out_5,
  output out_6,
  output out_7,
  output out_8
);

  wire not_1_out;

  not not_1 (not_1_out, in_1);
  and and_1 (out_5, in_1, not_1_out);

  assign out_6 = in_1;
  assign out_7 = in_2;
  assign out_8 = in_3;
endmodule

// SRL
module shift_right_logic (
  input  in_1,
  input  in_2,
  input  in_3,
  input  in_4,
  output out_5,
  output out_6,
  output out_7,
  output out_8
);

  wire not_1_out;

  not not_1 (not_1_out, in_4);
  and and_1 (out_8, in_4, not_1_out);

  assign out_5 = in_2;
  assign out_6 = in_3;
  assign out_7 = in_4;
endmodule

// SLA
module shift_left_arthmetic (
  input  in_1,
  input  in_2,
  input  in_3,
  input  in_4,
  output out_5,
  output out_6,
  output out_7,
  output out_8
);

  wire not_1_out;

  not not_1 (not_1_out, in_1);
  and and_1 (out_5, in_1, not_1_out);

  assign out_6 = in_1;
  assign out_7 = in_2;
  assign out_8 = in_3;
endmodule

// SRA
module shift_right_arthmetic (
  input  in_1,
  input  in_2,
  input  in_3,
  input  in_4,
  output out_5,
  output out_6,
  output out_7,
  output out_8
);


  assign out_5 = in_2;
  assign out_6 = in_3;
  assign out_7 = in_4;
  assign out_8 = in_4;
endmodule

// SRC
module shift_right_circular (
  input  in_1,
  input  in_2,
  input  in_3,
  input  in_4,
  output out_5,
  output out_6,
  output out_7,
  output out_8
);


  assign out_5 = in_2;
  assign out_6 = in_3;
  assign out_7 = in_4;
  assign out_8 = in_1;
endmodule

// SLC
module shift_left_circular (
  input  in_1,
  input  in_2,
  input  in_3,
  input  in_4,
  output out_5,
  output out_6,
  output out_7,
  output out_8
);


  assign out_5 = in_4;
  assign out_6 = in_1;
  assign out_7 = in_2;
  assign out_8 = in_3;
endmodule

// B-A
module sub_B_A (
  input  in_1,
  input  A0,
  input  A1,
  input  A2,
  input  A3,
  input  B0,
  input  B1,
  input  B2,
  input  B3,
  output out_10,
  output out_11,
  output out_12,
  output out_13,
  output out_14,
  output _1_if_B_A
);

  wire add_1_carry_2, n2_scomplement_1_w, n2_scomplement_1_x, n2_scomplement_1_y, n2_scomplement_1_z,
       not_1_out, or_1_out;

  _2_scomplement u_2_scomplement_1 (
    .D(A0), .C(A1), .B(A2), .A(A3), .Z(n2_scomplement_1_z), .Y(n2_scomplement_1_y), .X(n2_scomplement_1_x),
    .W(n2_scomplement_1_w));
  Add add_1 (
    .A0(n2_scomplement_1_z), .A1(n2_scomplement_1_y), .A2(n2_scomplement_1_x), .A3(n2_scomplement_1_w),
    .B0(B0), .B1(B1), .B2(B2), .B3(B3), .carry(in_1), .out_10(out_10), .out_11(out_11), .out_12(out_12),
    .out_13(out_13), .Carry_2(add_1_carry_2), .overflow(_1_if_B_A));
  or or_1 (or_1_out, A0, A1, A2, A3);
  not not_1 (not_1_out, add_1_carry_2);
  and and_1 (out_14, or_1_out, not_1_out);
endmodule

// A-B
module sub_A_B (
  input  in_1,
  input  A0,
  input  A1,
  input  A2,
  input  A3,
  input  B0,
  input  B1,
  input  B2,
  input  B3,
  output out_10,
  output out_11,
  output out_12,
  output out_13,
  output out_14,
  output out_15
);

  wire add_1_carry_2, n2_scomplement_1_w, n2_scomplement_1_x, n2_scomplement_1_y, n2_scomplement_1_z,
       not_1_out, or_1_out;

  _2_scomplement u_2_scomplement_1 (
    .D(B0), .C(B1), .B(B2), .A(B3), .Z(n2_scomplement_1_z), .Y(n2_scomplement_1_y), .X(n2_scomplement_1_x),
    .W(n2_scomplement_1_w));
  Add add_1 (
    .A0(A0), .A1(A1), .A2(A2), .A3(A3), .B0(n2_scomplement_1_z), .B1(n2_scomplement_1_y),
    .B2(n2_scomplement_1_x), .B3(n2_scomplement_1_w), .carry(in_1), .out_10(out_10), .out_11(out_11),
    .out_12(out_12), .out_13(out_13), .Carry_2(add_1_carry_2), .overflow(out_15));
  or or_1 (or_1_out, n2_scomplement_1_z, n2_scomplement_1_y, n2_scomplement_1_x, n2_scomplement_1_w);
  not not_1 (not_1_out, add_1_carry_2);
  and and_1 (out_14, not_1_out, or_1_out);
endmodule

// Multiply
module multiplier (
  input  in_1,
  input  A0,
  input  A1,
  input  A2,
  input  A3,
  input  B0,
  input  B1,
  input  B2,
  input  B3,
  output out_10,
  output out_11,
  output out_12,
  output out_13,
  output out_14,
  output out_15,
  output out_16,
  output out_17
);

  wire add_1_carry_2, add_1_out_11, add_1_out_12, add_1_out_13, add_2_carry_2, add_2_out_11, add_2_out_12,
       add_2_out_13, and_2_out, and_3_out, and_4_out, and_5_out, and_6_out, and_7_out, and_8_out, and_9_out,
       and_10_out, and_11_out, and_12_out, and_13_out, and_14_out, and_15_out, and_16_out;

  and and_1 (out_10, A0, B0);
  and and_2 (and_2_out, A1, B0);
  and and_3 (and_3_out, A2, B0);
  and and_4 (and_4_out, A3, B0);
  and and_5 (and_5_out, A0, B1);
  and and_6 (and_6_out, A1, A1, B1);
  and and_7 (and_7_out, A2, A2, B1);
  and and_8 (and_8_out, A3, A3, B1);
  Add add_1 (
    .A0(and_2_out), .A1(and_3_out), .A2(and_4_out), .A3(in_1), .B0(and_5_out), .B1(and_6_out),
    .B2(and_7_out), .B3(and_8_out), .carry(in_1), .out_10(out_11), .out_11(add_1_out_11),
    .out_12(add_1_out_12), .out_13(add_1_out_13), .Carry_2(add_1_carry_2));  // open: overflow
  and and_9 (and_9_out, A0, B2);
  and and_10 (and_10_out, B2, A1);
  and and_11 (and_11_out, B2, A2);
  and and_12 (and_12_out, B2, A3);
  Add add_2 (
    .A0(add_1_out_11), .A1(add_1_out_12), .A2(add_1_out_13), .A3(add_1_carry_2), .B0(and_9_out),
    .B1(and_10_out), .B2(and_11_out), .B3(and_12_out), .carry(in_1), .out_10(out_12), .out_11(add_2_out_11),
    .out_12(add_2_out_12), .out_13(add_2_out_13), .Carry_2(add_2_carry_2));  // open: overflow
  and and_13 (and_13_out, A0, B3);
  and and_14 (and_14_out, B3, A1);
  and and_15 (and_15_out, B3, A2);
  and and_16 (and_16_out, B3, A3);
  Add add_3 (
    .A0(add_2_out_11), .A1(add_2_out_12), .A2(add_2_out_13), .A3(add_2_carry_2), .B0(and_13_out),
    .B1(and_14_out), .B2(and_15_out), .B3(and_16_out), .carry(in_1), .out_10(out_13), .out_11(out_14),
    .out_12(out_15), .out_13(out_16), .Carry_2(out_17));  // open: overflow
endmodule

module ALU (
  input  [3:0] in_1,
  input  [3:0] A,
  input  [3:0] B,
  input  overflow,
  output [7:0] out_5,
  output out_6,
  output out_7,
  output out_8
);

  wire _3_out, A_B_out, add_1_carry_2, add_1_overflow, add_2_out, and_3_out, and_4_out, and_5_out,
       decoder_1_out0, decoder_1_out1, decoder_1_out2, decoder_1_out3, not_1_out, or_2_out, or_3_out,
       or_4_out, sub_a_b_1_out_14, sub_a_b_1_out_15, sub_b_a_1__1_if_b_a, sub_b_a_1_out_14;
  wire [3:0] add_1_out_10, and_1_w, n1_scomplement_1_out_5, n2_scomplement_1_z, nand_1_w, or_1_w,
       shift_left_arthmetic_1_out_5, shift_left_circular_1_out_5, shift_left_logic_1_out_5,
       shift_right_arthmetic_1_out_5, shift_right_circular_1_out_5, shift_right_logic_1_out_5,
       sub_a_b_1_out_10, sub_b_a_1_out_10, xor_1_w;
  wire [7:0] multiplier_1_out_10;

  Add add_1 (
    .A0(A[0]), .A1(A[1]), .A2(A[2]), .A3(A[3]), .B0(B[0]), .B1(B[1]), .B2(B[2]), .B3(B[3]), .carry(overflow),
    .out_10(add_1_out_10[0]), .out_11(add_1_out_10[1]), .out_12(add_1_out_10[2]), .out_13(add_1_out_10[3]),
    .Carry_2(add_1_carry_2), .overflow(add_1_overflow));
  _1_scomplement u_1_scomplement_1 (
    .A(A[3]), .B(A[2]), .C(A[1]), .D(A[0]), .out_5(n1_scomplement_1_out_5[0]),
    .out_6(n1_scomplement_1_out_5[1]), .out_7(n1_scomplement_1_out_5[2]), .out_8(n1_scomplement_1_out_5[3]));
  _2_scomplement u_2_scomplement_1 (
    .D(A[3]), .C(A[2]), .B(A[1]), .A(A[0]), .Z(n2_scomplement_1_z[0]), .Y(n2_scomplement_1_z[1]),
    .X(n2_scomplement_1_z[2]), .W(n2_scomplement_1_z[3]));
  sub_A_B sub_a_b_1 (
    .A0(A[0]), .A1(A[1]), .A2(A[2]), .A3(A[3]), .B0(B[0]), .B1(B[1]), .B2(B[2]), .B3(B[3]), .in_1(overflow),
    .out_10(sub_a_b_1_out_10[0]), .out_11(sub_a_b_1_out_10[1]), .out_12(sub_a_b_1_out_10[2]),
    .out_13(sub_a_b_1_out_10[3]), .out_14(sub_a_b_1_out_14), .out_15(sub_a_b_1_out_15));
  shift_left_logic shift_left_logic_1 (
    .in_1(A[3]), .in_2(A[2]), .in_3(A[1]), .in_4(A[0]), .out_5(shift_left_logic_1_out_5[0]),
    .out_6(shift_left_logic_1_out_5[1]), .out_7(shift_left_logic_1_out_5[2]),
    .out_8(shift_left_logic_1_out_5[3]));
  sub_B_A sub_b_a_1 (
    .A0(A[0]), .A1(A[1]), .A2(A[2]), .A3(A[3]), .B0(B[0]), .B1(B[1]), .B2(B[2]), .B3(B[3]), .in_1(overflow),
    .out_10(sub_b_a_1_out_10[0]), .out_11(sub_b_a_1_out_10[1]), .out_12(sub_b_a_1_out_10[2]),
    .out_13(sub_b_a_1_out_10[3]), .out_14(sub_b_a_1_out_14), ._1_if_B_A(sub_b_a_1__1_if_b_a));
  shift_right_logic shift_right_logic_1 (
    .in_1(A[3]), .in_2(A[2]), .in_3(A[1]), .in_4(A[0]), .out_5(shift_right_logic_1_out_5[0]),
    .out_6(shift_right_logic_1_out_5[1]), .out_7(shift_right_logic_1_out_5[2]),
    .out_8(shift_right_logic_1_out_5[3]));
  shift_left_arthmetic shift_left_arthmetic_1 (
    .in_1(A[3]), .in_2(A[2]), .in_3(A[1]), .in_4(A[0]), .out_5(shift_left_arthmetic_1_out_5[0]),
    .out_6(shift_left_arthmetic_1_out_5[1]), .out_7(shift_left_arthmetic_1_out_5[2]),
    .out_8(shift_left_arthmetic_1_out_5[3]));
  shift_right_arthmetic shift_right_arthmetic_1 (
    .in_1(A[3]), .in_2(A[2]), .in_3(A[1]), .in_4(A[0]), .out_5(shift_right_arthmetic_1_out_5[0]),
    .out_6(shift_right_arthmetic_1_out_5[1]), .out_7(shift_right_arthmetic_1_out_5[2]),
    .out_8(shift_right_arthmetic_1_out_5[3]));
  shift_left_circular shift_left_circular_1 (
    .in_1(A[3]), .in_2(A[2]), .in_3(A[1]), .in_4(A[0]), .out_5(shift_left_circular_1_out_5[0]),
    .out_6(shift_left_circular_1_out_5[1]), .out_7(shift_left_circular_1_out_5[2]),
    .out_8(shift_left_circular_1_out_5[3]));
  multiplier multiplier_1 (
    .A0(A[0]), .A1(A[1]), .A2(A[2]), .A3(A[3]), .B0(B[0]), .B1(B[1]), .B2(B[2]), .B3(B[3]), .in_1(overflow),
    .out_10(multiplier_1_out_10[0]), .out_11(multiplier_1_out_10[1]), .out_12(multiplier_1_out_10[2]),
    .out_13(multiplier_1_out_10[3]), .out_14(multiplier_1_out_10[4]), .out_15(multiplier_1_out_10[5]),
    .out_16(multiplier_1_out_10[6]), .out_17(multiplier_1_out_10[7]));
  shift_right_circular shift_right_circular_1 (
    .in_1(A[3]), .in_2(A[2]), .in_3(A[1]), .in_4(A[0]), .out_5(shift_right_circular_1_out_5[0]),
    .out_6(shift_right_circular_1_out_5[1]), .out_7(shift_right_circular_1_out_5[2]),
    .out_8(shift_right_circular_1_out_5[3]));
  \and  and_1 (
    .A0(A[0]), .A1(A[1]), .A2(A[2]), .A3(A[3]), .B0(B[0]), .B1(B[1]), .B2(B[2]), .B3(B[3]), .W(and_1_w[0]),
    .X(and_1_w[1]), .Y(and_1_w[2]), .Z(and_1_w[3]));
  \or  or_1 (
    .A0(A[0]), .A1(A[1]), .A2(A[2]), .A3(A[3]), .B0(B[0]), .B1(B[1]), .B2(B[2]), .B3(B[3]), .W(or_1_w[0]),
    .X(or_1_w[1]), .Y(or_1_w[2]), .Z(or_1_w[3]));
  \xor  xor_1 (
    .A0(A[0]), .A1(A[1]), .A2(A[2]), .A3(A[3]), .B0(B[0]), .B1(B[1]), .B2(B[2]), .B3(B[3]), .W(xor_1_w[0]),
    .X(xor_1_w[1]), .Y(xor_1_w[2]), .Z(xor_1_w[3]));
  \nand  nand_1 (
    .A0(A[0]), .A1(A[1]), .A2(A[2]), .A3(A[3]), .B0(B[0]), .B1(B[1]), .B2(B[2]), .B3(B[3]), .W(nand_1_w[0]),
    .X(nand_1_w[1]), .Y(nand_1_w[2]), .Z(nand_1_w[3]));
  Decoder #(.select(4), .enable("false")) decoder_1 (
    .out0(decoder_1_out0), .out1(decoder_1_out1), .out2(decoder_1_out2), .out3(decoder_1_out3), .sel(in_1));  // open: out4, out5, out6, out7, out8, out9, out10, out11, out12, out13, out14, out15
  or or_2 (or_2_out, decoder_1_out0, decoder_1_out1, decoder_1_out2, decoder_1_out3);
  Multiplexer #(.select(4), .width(8), .enable("false")) multiplexer_1 (
    .in0({{4{overflow}}, add_1_out_10}), .in1({{4{overflow}}, sub_a_b_1_out_10}),
    .in2({{4{overflow}}, sub_b_a_1_out_10}), .in3(multiplier_1_out_10), .in4({{4{overflow}}, and_1_w}),
    .in5({{4{overflow}}, or_1_w}), .in6({{4{overflow}}, xor_1_w}), .in7({{4{overflow}}, nand_1_w}),
    .in8({{4{overflow}}, n2_scomplement_1_z}), .in9({{4{overflow}}, n1_scomplement_1_out_5}),
    .in10({{4{overflow}}, shift_left_logic_1_out_5}), .in11({{4{overflow}}, shift_right_logic_1_out_5}),
    .in12({{4{overflow}}, shift_left_arthmetic_1_out_5}),
    .in13({{4{overflow}}, shift_right_arthmetic_1_out_5}),
    .in14({{4{overflow}}, shift_left_circular_1_out_5}),
    .in15({{4{overflow}}, shift_right_circular_1_out_5}), .out(out_5), .sel(in_1));
  or or_3 (or_3_out, out_5[3], out_5[2], out_5[1], out_5[0]);
  or or_4 (or_4_out, out_5[7], out_5[6], out_5[5], out_5[4], or_3_out);
  not not_1 (not_1_out, or_4_out);
  and _3 (_3_out, decoder_1_out2, sub_b_a_1_out_14);
  and add_2 (add_2_out, decoder_1_out0, add_1_carry_2);
  and A_B (A_B_out, decoder_1_out1, sub_a_b_1_out_14);
  or or_5 (out_7, A_B_out, add_2_out, _3_out);
  and and_2 (out_6, or_2_out, not_1_out);
  and and_3 (and_3_out, decoder_1_out2, sub_a_b_1_out_15);
  and and_4 (and_4_out, decoder_1_out0, add_1_overflow);
  and and_5 (and_5_out, decoder_1_out1, sub_b_a_1__1_if_b_a);
  or or_6 (out_8, and_5_out, and_4_out, and_3_out);

  // Notes on the sheet:
  //   carry
  //   1
  //   2
  //   B-A
endmodule
